// Logisim project PROIECT_LOGISIM.circ as structural Verilog: 12 circuits, main circuit cnt6
module main (
  input  ALARM,
  input  SET,
  input  START,
  input  RDO
);

  wire aparat_1_alarm_on, aparat_1_radio_2, aparat_1_ringalarm, clock_1_out, H_out, M_out, RESET_out,
       STOP_ALARM_out;
  wire [6:0] aparat_1_uctdhour, aparat_1_uctdmin, aparat_1_zctdhour, aparat_1_zctdmin;

  Button STOP_ALARM (.out(STOP_ALARM_out));
  Button RESET (.out(RESET_out));
  Clock clock_1 (.out(clock_1_out));
  _7_Segment_Display u_7_segment_display_1 (
    .g(aparat_1_zctdhour[2]), .f(aparat_1_zctdhour[1]), .a(aparat_1_zctdhour[0]), .b(aparat_1_zctdhour[3]),
    .e(aparat_1_zctdhour[6]), .d(aparat_1_zctdhour[5]), .c(aparat_1_zctdhour[4]));  // open: dp
  Button M (.out(M_out));
  Button H (.out(H_out));
  aparat aparat_1 (
    .ALARM(ALARM), .SET(SET), .STOPALARM(STOP_ALARM_out), .CLK(clock_1_out), .RST(RESET_out), .START(START),
    .RADIO(RDO), .M(M_out), .H(H_out), .ZCTDHOUR(aparat_1_zctdhour), .UCTDHOUR(aparat_1_uctdhour),
    .ZCTDMIN(aparat_1_zctdmin), .UCTDMIN(aparat_1_uctdmin), .RINGALARM(aparat_1_ringalarm),
    .RADIO_2(aparat_1_radio_2), .ALARM_ON(aparat_1_alarm_on));
  _7_Segment_Display u_7_segment_display_2 (
    .g(aparat_1_uctdhour[2]), .f(aparat_1_uctdhour[1]), .a(aparat_1_uctdhour[0]), .b(aparat_1_uctdhour[3]),
    .e(aparat_1_uctdhour[6]), .d(aparat_1_uctdhour[5]), .c(aparat_1_uctdhour[4]));  // open: dp
  _7_Segment_Display u_7_segment_display_3 (
    .g(aparat_1_zctdmin[2]), .f(aparat_1_zctdmin[1]), .a(aparat_1_zctdmin[0]), .b(aparat_1_zctdmin[3]),
    .e(aparat_1_zctdmin[6]), .d(aparat_1_zctdmin[5]), .c(aparat_1_zctdmin[4]));  // open: dp
  LED u_ALARM (.in(aparat_1_ringalarm));
  LED RADIO (.in(aparat_1_radio_2));
  _7_Segment_Display u_7_segment_display_4 (
    .g(aparat_1_uctdmin[2]), .f(aparat_1_uctdmin[1]), .a(aparat_1_uctdmin[0]), .b(aparat_1_uctdmin[3]),
    .e(aparat_1_uctdmin[6]), .d(aparat_1_uctdmin[5]), .c(aparat_1_uctdmin[4]), .dp(aparat_1_alarm_on));
endmodule

module cnt6 (
  input  EN,
  input  CLK,
  input  RST,
  output CARRY,
  output [3:0] Q
);

  wire and_1_out, and_2_out, not_1_out, not_2_out, not_3_out, not_4_out, or_1_out;

  Counter #(.width(4), .max('hf)) counter_1 (.Q(Q), .clk(and_1_out), .clr(or_1_out));  // open: load, D, count, carry
  and and_1 (and_1_out, EN, CLK);
  not not_1 (not_1_out, Q[0]);
  not not_2 (not_2_out, Q[3]);
  and and_2 (and_2_out, not_1_out, Q[1], Q[2], not_2_out);
  not not_3 (not_3_out, Q[0]);
  not not_4 (not_4_out, Q[3]);
  or or_1 (or_1_out, and_2_out, RST);
  and and_3 (CARRY, not_3_out, Q[1], Q[2], not_4_out);
endmodule

module cnt10 (
  input  EN,
  input  CLK,
  input  RST,
  output CARRY,
  output [3:0] Q
);

  wire and_1_out, and_2_out, not_1_out, not_2_out, not_3_out, not_4_out, or_1_out;

  and and_1 (and_1_out, EN, CLK);
  Counter #(.width(4), .max('hf)) counter_1 (.Q(Q), .clk(and_1_out), .clr(or_1_out));  // open: load, D, count, carry
  not not_1 (not_1_out, Q[0]);
  not not_2 (not_2_out, Q[2]);
  and and_2 (and_2_out, not_1_out, Q[1], not_2_out, Q[3]);
  not not_3 (not_3_out, Q[0]);
  not not_4 (not_4_out, Q[2]);
  or or_1 (or_1_out, and_2_out, RST);
  and and_3 (CARRY, not_3_out, Q[1], not_4_out, Q[3]);
endmodule

module cnt3 (
  input  EN,
  input  CLK,
  input  RST,
  output CARRY,
  output [3:0] Q
);

  wire and_1_out, and_2_out, not_1_out, not_2_out, not_3_out, not_4_out, not_5_out, or_1_out;

  and and_1 (and_1_out, EN, CLK);
  Counter #(.width(4), .max('hf)) counter_1 (.Q(Q), .clk(and_1_out), .clr(or_1_out));  // open: load, D, count, carry
  and and_2 (and_2_out, Q[0], Q[1], not_1_out, not_2_out);
  not not_1 (not_1_out, Q[2]);
  not not_2 (not_2_out, Q[3]);
  not not_3 (not_3_out, Q[0]);
  not not_4 (not_4_out, Q[2]);
  not not_5 (not_5_out, Q[3]);
  or or_1 (or_1_out, and_2_out, RST);
  and and_3 (CARRY, not_3_out, Q[1], not_4_out, not_5_out);
endmodule

module DCD7SEG (
  input  A,
  input  B,
  input  C,
  input  D,
  output a_2,
  output f,
  output g,
  output b_2,
  output c_2,
  output d_2,
  output e
);

  wire and_1_out, and_2_out, and_3_out, and_4_out, and_5_out, and_6_out, and_7_out, and_8_out, and_9_out,
       and_10_out, and_11_out, not_1_out, not_2_out, not_3_out, not_4_out, not_5_out, not_6_out, not_7_out,
       not_8_out, not_9_out, not_10_out, not_11_out;

  not not_1 (not_1_out, B);
  not not_2 (not_2_out, D);
  not not_3 (not_3_out, D);
  not not_4 (not_4_out, B);
  not not_5 (not_5_out, D);
  not not_6 (not_6_out, C);
  and and_1 (and_1_out, not_1_out, not_3_out);
  and and_2 (and_2_out, C, not_3_out);
  and and_3 (and_3_out, not_4_out, not_5_out);
  and and_4 (and_4_out, D, B);
  not not_7 (not_7_out, B);
  not not_8 (not_8_out, C);
  and and_5 (and_5_out, not_8_out, not_9_out);
  not not_9 (not_9_out, D);
  and and_6 (and_6_out, D, C);
  not not_10 (not_10_out, C);
  or or_1 (c_2, not_10_out, D, B);
  and and_7 (and_7_out, not_1_out, not_2_out);
  and and_8 (and_8_out, not_1_out, C);
  and and_9 (and_9_out, not_6_out, B, D);
  or or_2 (e, and_1_out, and_2_out);
  or or_3 (a_2, and_3_out, A, C, and_4_out);
  and and_10 (and_10_out, B, not_8_out);
  or or_4 (b_2, not_7_out, and_5_out, and_6_out);
  not not_11 (not_11_out, D);
  or or_5 (d_2, and_7_out, and_8_out, and_9_out, A, and_2_out);
  and and_11 (and_11_out, B, not_11_out);
  or or_6 (f, A, and_11_out, and_10_out, and_5_out);
  or or_7 (g, A, and_11_out, and_10_out, and_8_out);
endmodule

module Detect4 (
  input  [3:0] _4b,
  input  [3:0] _2b,
  output out_3
);

  wire and_1_out, and_2_out, not_1_out, not_2_out, not_3_out, not_4_out, not_5_out, not_6_out;

  not not_1 (not_1_out, _4b[0]);
  not not_2 (not_2_out, _4b[1]);
  not not_3 (not_3_out, _4b[3]);
  not not_4 (not_4_out, _2b[0]);
  not not_5 (not_5_out, _2b[2]);
  not not_6 (not_6_out, _2b[3]);
  and and_1 (and_1_out, not_1_out, not_2_out, _4b[2], not_3_out);
  and and_2 (and_2_out, not_4_out, _2b[1], not_5_out, not_6_out);
  and and_3 (out_3, and_1_out, and_2_out);
endmodule

module modul_numarare (
  input  EN,
  input  CLK,
  input  M,
  input  SET,
  input  RST,
  input  H,
  output [3:0] UHOUR,
  output [3:0] ZHOUR,
  output [3:0] UMIN,
  output [3:0] ZMIN
);

  wire cnt6_1_carry, cnt6_2_carry, cnt10_1_carry, cnt10_2_carry, cnt10_3_carry, detect4_1_out_3,
       multiplexer_1_out, multiplexer_2_out, or_1_out;

  cnt6 cnt6_1 (.EN(EN), .CLK(cnt10_1_carry), .RST(RST), .CARRY(cnt6_1_carry));  // open: Q
  cnt10 cnt10_1 (.EN(EN), .CLK(CLK), .RST(RST), .CARRY(cnt10_1_carry));  // open: Q
  Multiplexer multiplexer_1 (.in0(cnt6_1_carry), .in1(M), .out(multiplexer_1_out), .sel(SET));  // open: en
  cnt10 cnt10_2 (.EN(EN), .CLK(multiplexer_1_out), .RST(RST), .CARRY(cnt10_2_carry), .Q(UMIN));
  cnt6 cnt6_2 (.EN(EN), .CLK(cnt10_2_carry), .RST(RST), .CARRY(cnt6_2_carry), .Q(ZMIN));
  Multiplexer multiplexer_2 (.in0(cnt6_2_carry), .in1(H), .out(multiplexer_2_out), .sel(SET));  // open: en
  cnt10 cnt10_3 (.EN(EN), .CLK(multiplexer_2_out), .RST(or_1_out), .CARRY(cnt10_3_carry), .Q(UHOUR));
  Detect4 detect4_1 (._4b(UHOUR), ._2b(ZHOUR), .out_3(detect4_1_out_3));
  cnt3 cnt3_1 (.EN(EN), .CLK(cnt10_3_carry), .RST(or_1_out), .Q(ZHOUR));  // open: CARRY
  or or_1 (or_1_out, detect4_1_out_3, RST);
endmodule

module modul_afisare (
  input  [3:0] ZHOUR,
  input  [3:0] UHOUR,
  input  [3:0] ZMIN,
  input  [3:0] UMIN,
  output [6:0] ZCTDHOUR,
  output [6:0] UCTDHOUR,
  output [6:0] ZCTDMIN,
  output [6:0] UCTDMIN
);

  DCD7SEG dcd7seg_1 (
    .A(ZHOUR[3]), .B(ZHOUR[2]), .C(ZHOUR[1]), .D(ZHOUR[0]), .a_2(ZCTDHOUR[0]), .f(ZCTDHOUR[1]),
    .g(ZCTDHOUR[2]), .b_2(ZCTDHOUR[3]), .c_2(ZCTDHOUR[4]), .d_2(ZCTDHOUR[5]), .e(ZCTDHOUR[6]));
  DCD7SEG dcd7seg_2 (
    .A(UHOUR[3]), .B(UHOUR[2]), .C(UHOUR[1]), .D(UHOUR[0]), .a_2(UCTDHOUR[0]), .f(UCTDHOUR[1]),
    .g(UCTDHOUR[2]), .b_2(UCTDHOUR[3]), .c_2(UCTDHOUR[4]), .d_2(UCTDHOUR[5]), .e(UCTDHOUR[6]));
  DCD7SEG dcd7seg_3 (
    .A(ZMIN[3]), .B(ZMIN[2]), .C(ZMIN[1]), .D(ZMIN[0]), .a_2(ZCTDMIN[0]), .f(ZCTDMIN[1]), .g(ZCTDMIN[2]),
    .b_2(ZCTDMIN[3]), .c_2(ZCTDMIN[4]), .d_2(ZCTDMIN[5]), .e(ZCTDMIN[6]));
  DCD7SEG dcd7seg_4 (
    .A(UMIN[3]), .B(UMIN[2]), .C(UMIN[1]), .D(UMIN[0]), .a_2(UCTDMIN[0]), .f(UCTDMIN[1]), .g(UCTDMIN[2]),
    .b_2(UCTDMIN[3]), .c_2(UCTDMIN[4]), .d_2(UCTDMIN[5]), .e(UCTDMIN[6]));
endmodule

module modul_comparare (
  input  [3:0] UTMIN,
  input  [3:0] UAMIN,
  input  [3:0] ZTMIN,
  input  [3:0] ZAMIN,
  input  [3:0] UTHOUR,
  input  [3:0] UAHOUR,
  input  [3:0] ZTHOUR,
  input  [3:0] ZAHOUR,
  output COMPARARE
);

  wire comparator_1_eq, comparator_2_eq, comparator_3_eq, comparator_4_eq;

  Comparator #(.width(4), .mode("unsigned")) comparator_1 (.a(UTMIN), .b(UAMIN), .eq(comparator_1_eq));  // open: gt, lt
  Comparator #(.width(4), .mode("unsigned")) comparator_2 (.a(ZTMIN), .b(ZAMIN), .eq(comparator_2_eq));  // open: gt, lt
  Comparator #(.width(4), .mode("unsigned")) comparator_3 (
    .a(UTHOUR), .b(UAHOUR), .eq(comparator_3_eq));  // open: gt, lt
  Comparator #(.width(4), .mode("unsigned")) comparator_4 (
    .a(ZTHOUR), .b(ZAHOUR), .eq(comparator_4_eq));  // open: gt, lt
  and and_1 (COMPARARE, comparator_1_eq, comparator_2_eq, comparator_3_eq, comparator_4_eq);
endmodule

module modul_alarma (
  input  STOPALARM,
  input  SETALARM,
  input  CLK,
  input  M,
  input  RST,
  input  H,
  output ALARM_ON,
  output [3:0] UAMIN,
  output [3:0] ZAMIN,
  output [3:0] UAHOUR,
  output [3:0] ZAHOUR
);

  wire and_1_out, or_1_out;

  modul_numarare modul_numarare_1 (
    .EN(SETALARM), .CLK(CLK), .M(M), .SET(1'b1), .RST(or_1_out), .H(H), .UMIN(UAMIN), .ZMIN(ZAMIN),
    .UHOUR(UAHOUR), .ZHOUR(ZAHOUR));
  D_Flip_Flop d_ff_1 (.clk(SETALARM), .D(SETALARM), .Q(ALARM_ON), .en(SETALARM), .reset(or_1_out));  // open: Qn, preset
  and and_1 (and_1_out, STOPALARM, ALARM_ON);
  or or_1 (or_1_out, and_1_out, RST);
endmodule

module UC (
  input  Alarm,
  input  Comp,
  input  Set,
  input  StopAlarm,
  input  CLK,
  input  RST,
  output AFISARE,
  output SETTIME,
  output SETALARM,
  output RINGALARM
);

  wire and_4_out, and_5_out, and_6_out, and_7_out, and_8_out, d_ff_1_q, d_ff_2_q, d_ff_2_qn, not_1_out,
       not_2_out, not_3_out, not_4_out, not_5_out, not_6_out, not_7_out, not_8_out, or_1_out, or_2_out,
       or_3_out;

  not not_1 (not_1_out, StopAlarm);
  and and_1 (AFISARE, d_ff_1_q, d_ff_2_qn);
  not not_2 (not_2_out, d_ff_1_q);
  not not_3 (not_3_out, d_ff_2_qn);
  and and_2 (SETTIME, not_2_out, not_3_out);
  not not_4 (not_4_out, Alarm);
  not not_5 (not_5_out, d_ff_2_qn);
  and and_3 (RINGALARM, not_4_out, not_5_out, d_ff_1_q, not_6_out);
  not not_6 (not_6_out, Set);
  and and_4 (and_4_out, Alarm, d_ff_1_q, d_ff_2_q, not_1_out);
  not not_7 (not_7_out, Alarm);
  or or_1 (or_1_out, Alarm, and_5_out, and_4_out);
  and and_5 (and_5_out, Comp, not_7_out);
  D_Flip_Flop d_ff_1 (.clk(CLK), .D(or_1_out), .Q(d_ff_1_q), .reset(or_2_out));  // open: Qn, preset, en
  not not_8 (not_8_out, Set);
  and and_6 (and_6_out, not_8_out, Comp);
  and and_7 (and_7_out, 1'b1, Set, Alarm);
  and and_8 (and_8_out, Set, d_ff_2_q, d_ff_1_q, not_1_out);
  or or_2 (or_2_out, and_7_out, RST);
  or or_3 (or_3_out, Set, and_6_out, and_8_out);
  D_Flip_Flop d_ff_2 (.clk(CLK), .D(or_3_out), .Q(d_ff_2_q), .Qn(d_ff_2_qn), .reset(or_2_out));  // open: preset, en

  assign SETALARM = AFISARE;
endmodule

module aparat (
  input  M,
  input  H,
  input  ALARM,
  input  SET,
  input  STOPALARM,
  input  CLK,
  input  RST,
  input  START,
  input  RADIO,
  output RINGALARM,
  output RADIO_2,
  output ALARM_ON,
  output [6:0] ZCTDHOUR,
  output [6:0] UCTDHOUR,
  output [6:0] ZCTDMIN,
  output [6:0] UCTDMIN
);

  wire and_1_out, Divizior_frecventa_carry, modul_alarma_1_alarm_on, modul_comparare_1_comparare,
       multiplexer_1_out, not_1_out, not_2_out, uc_1_afisare, uc_1_ringalarm, uc_1_setalarm, uc_1_settime;
  wire [3:0] modul_alarma_1_uahour, modul_alarma_1_uamin, modul_alarma_1_zahour, modul_alarma_1_zamin,
       modul_numarare_1_uhour, modul_numarare_1_umin, modul_numarare_1_zhour, modul_numarare_1_zmin;
  wire [6:0] modul_afisare_1_uctdhour, modul_afisare_1_uctdmin, modul_afisare_1_zctdhour,
       modul_afisare_1_zctdmin, modul_afisare_2_uctdhour, modul_afisare_2_uctdmin, modul_afisare_2_zctdhour,
       modul_afisare_2_zctdmin;

  Multiplexer multiplexer_1 (
    .in0(1'b0), .in1(and_1_out), .out(multiplexer_1_out), .sel(modul_alarma_1_alarm_on), .en(START));
  and and_1 (and_1_out, modul_comparare_1_comparare, not_2_out, not_1_out);
  not not_1 (not_1_out, SET);
  not not_2 (not_2_out, ALARM);
  UC uc_1 (
    .Alarm(ALARM), .Comp(multiplexer_1_out), .Set(SET), .StopAlarm(STOPALARM), .CLK(CLK), .RST(RST),
    .AFISARE(uc_1_afisare), .SETTIME(uc_1_settime), .SETALARM(uc_1_setalarm), .RINGALARM(uc_1_ringalarm));
  Counter #(.width(3), .max('h4)) Divizior_frecventa (
    .carry(Divizior_frecventa_carry), .clk(CLK));  // open: load, D, count, Q, clr
  modul_comparare modul_comparare_1 (
    .UTMIN(modul_numarare_1_umin), .UAMIN(modul_alarma_1_uamin), .ZTMIN(modul_numarare_1_zmin),
    .ZAMIN(modul_alarma_1_zamin), .UTHOUR(modul_numarare_1_uhour), .UAHOUR(modul_alarma_1_uahour),
    .ZTHOUR(modul_numarare_1_zhour), .ZAHOUR(modul_alarma_1_zahour), .COMPARARE(modul_comparare_1_comparare));
  modul_numarare modul_numarare_1 (
    .EN(1'b1), .CLK(Divizior_frecventa_carry), .M(M), .SET(uc_1_settime), .RST(RST), .H(H),
    .UMIN(modul_numarare_1_umin), .ZMIN(modul_numarare_1_zmin), .UHOUR(modul_numarare_1_uhour),
    .ZHOUR(modul_numarare_1_zhour));
  modul_afisare modul_afisare_1 (
    .ZHOUR(modul_numarare_1_zhour), .UHOUR(modul_numarare_1_uhour), .ZMIN(modul_numarare_1_zmin),
    .UMIN(modul_numarare_1_umin), .ZCTDHOUR(modul_afisare_1_zctdhour), .UCTDHOUR(modul_afisare_1_uctdhour),
    .ZCTDMIN(modul_afisare_1_zctdmin), .UCTDMIN(modul_afisare_1_uctdmin));
  Multiplexer #(.width(7)) multiplexer_2 (
    .in0(modul_afisare_1_zctdhour), .in1(modul_afisare_2_zctdhour), .out(ZCTDHOUR), .sel(uc_1_afisare),
    .en(START));
  Multiplexer #(.width(7)) multiplexer_3 (
    .in0(modul_afisare_1_uctdhour), .in1(modul_afisare_2_uctdhour), .out(UCTDHOUR), .sel(uc_1_afisare),
    .en(START));
  Multiplexer #(.width(7)) multiplexer_4 (
    .in0(modul_afisare_1_zctdmin), .in1(modul_afisare_2_zctdmin), .out(ZCTDMIN), .sel(uc_1_afisare),
    .en(START));
  modul_alarma modul_alarma_1 (
    .STOPALARM(STOPALARM), .SETALARM(uc_1_setalarm), .CLK(CLK), .M(M), .RST(RST), .H(H),
    .ALARM_ON(modul_alarma_1_alarm_on), .UAMIN(modul_alarma_1_uamin), .ZAMIN(modul_alarma_1_zamin),
    .UAHOUR(modul_alarma_1_uahour), .ZAHOUR(modul_alarma_1_zahour));
  modul_afisare modul_afisare_2 (
    .ZHOUR(modul_alarma_1_zahour), .UHOUR(modul_alarma_1_uahour), .ZMIN(modul_alarma_1_zamin),
    .UMIN(modul_alarma_1_uamin), .ZCTDHOUR(modul_afisare_2_zctdhour), .UCTDHOUR(modul_afisare_2_uctdhour),
    .ZCTDMIN(modul_afisare_2_zctdmin), .UCTDMIN(modul_afisare_2_uctdmin));
  Multiplexer #(.width(7)) multiplexer_5 (
    .in0(modul_afisare_1_uctdmin), .in1(modul_afisare_2_uctdmin), .out(UCTDMIN), .sel(uc_1_afisare),
    .en(START));
  and and_2 (RINGALARM, modul_alarma_1_alarm_on, uc_1_ringalarm, START);
  and and_3 (RADIO_2, START, RADIO);
  and and_4 (ALARM_ON, modul_alarma_1_alarm_on, START);
endmodule
